// Logisim project cpu.circ as structural Verilog: 1 circuit, main circuit cpu
module cpu (
  input  clk,
  input  [31:0] Instruction,
  input  [31:0] MemReadData,
  output [31:0] MemAddress,
  output [31:0] ProgramCounter,
  output [31:0] ra,
  output [31:0] sp,
  output [31:0] t0,
  output [31:0] t1,
  output [31:0] t2,
  output [31:0] s0,
  output [31:0] s1,
  output [31:0] a0,
  output [3:0] MemWriteMask,
  output [31:0] MemWriteData
);

  wire ASel, BrEq, BrLt, BrUn, BSel, comparator_1_eq, comparator_1_lt, comparator_2_eq, comparator_2_lt,
       RegWEn;
  wire [1:0] WBSel;
  wire [2:0] ImmSel;
  wire [3:0] ALUSel;
  wire [31:0] A, A1, adder_1_out, ALUResult, B, B1, B2, undriven, WB;

  Adder #(.width(32)) adder_1 (.a(ProgramCounter), .b(32'h4), .out(adder_1_out));  // open: cin, cout
  Register #(.width(32)) PC (.D(adder_1_out), .clk(clk), .Q(ProgramCounter));  // open: en, clr
  control_logic control_logic_1 (
    .Instruction(Instruction), .BrEq(BrEq), .BrLt(BrLt), .RegWEn(RegWEn), .ImmSel(ImmSel), .BrUn(BrUn),
    .ASel(ASel), .BSel(BSel), .ALUSel(ALUSel), .WBSel(WBSel));  // open: PCSel, MemWEn
  regfile regfile_1 (
    .ReadIndex1(Instruction[19:15]), .ReadIndex2(Instruction[24:20]), .WriteIndex(Instruction[11:7]),
    .WriteData(WB), .RegWEn(RegWEn), .clk(clk), .ra(ra), .sp(sp), .t0(t0), .t1(t1), .t2(t2), .s0(s0),
    .s1(s1), .a0(a0), .ReadData1(A1), .ReadData2(B1));
  Comparator #(.width(32)) comparator_1 (.a(A1), .b(B1), .eq(comparator_1_eq), .lt(comparator_1_lt));  // open: gt
  Comparator #(.mode("unsigned"), .width(32)) comparator_2 (
    .a(A1), .b(B1), .eq(comparator_2_eq), .lt(comparator_2_lt));  // open: gt
  Multiplexer multiplexer_1 (.in0(comparator_1_eq), .in1(comparator_2_eq), .out(BrEq), .sel(BrUn));
  Multiplexer multiplexer_2 (.in0(comparator_1_lt), .in1(comparator_2_lt), .out(BrLt), .sel(BrUn));
  imm_gen imm_gen_1 (.Instruction(Instruction), .ImmSel(ImmSel), .Immediate(B2));
  Multiplexer #(.width(32)) multiplexer_3 (.in0(A1), .in1(ProgramCounter), .out(A), .sel(ASel));
  Multiplexer #(.width(32)) multiplexer_4 (.in0(B1), .in1(B2), .out(B), .sel(BSel));
  alu alu_1 (.A(A), .B(B), .ALUSel(ALUSel), .ALUResult(ALUResult));
  Multiplexer #(.select(2), .width(32)) multiplexer_5 (
    .in0(undriven), .in1(ALUResult), .out(WB), .sel(WBSel));  // open: in2, in3
  // branch_comp branch_comp_1: pin names not known
  partial_store partial_store_1 (
    .Instruction(Instruction), .MemAddress(ALUResult));  // open: DataFromReg, MemWEn, MemWriteMask, DataToMem
  partial_load partial_load_1 (.Instruction(Instruction), .MemAddress(ALUResult));  // open: DataFromMem, DataToReg

  // Notes on the sheet:
  //   To IMEM
  //   IMEM (do **NOT** move this)
  //   From IMEM
  //   Inputs/Outputs for testing. Do **NOT** move these.
  //   To DMEM
  //   DMEM (do **NOT** move this)
  //   From DMEM
endmodule
