// Logisim project regfile.circ as structural Verilog: 1 circuit, main circuit regfile
module regfile (
  input  [4:0] ReadIndex1,
  input  [4:0] ReadIndex2,
  input  [4:0] WriteIndex,
  input  [31:0] WriteData,
  input  RegWEn,
  input  clk,
  output [31:0] ra,
  output [31:0] sp,
  output [31:0] t0,
  output [31:0] t1,
  output [31:0] t2,
  output [31:0] s0,
  output [31:0] s1,
  output [31:0] a0,
  output [31:0] ReadData1,
  output [31:0] ReadData2
);

  wire [31:0] D0, D1, D2, D3, D4, D5, D6, D7, D8, D9, D10, D11, D12, D13, D14, D15, D16, D17, D18, D19, D20,
       D21, D22, D23, D24, D25, D26, D27, D28, D29, D30, D31, x0, x3, x4, x11, x12, x13, x14, x15, x16, x17,
       x18, x19, x20, x21, x22, x23, x24, x25, x26, x27, x28, x29, x30, x31;

  Register #(.width(32)) u_x0 (.D(D0), .clk(clk), .Q(x0));  // open: en, clr
  Register #(.width(32)) register_1 (.D(D1), .en(RegWEn), .clk(clk), .Q(ra));  // open: clr
  Register #(.width(32)) register_2 (.D(D2), .en(RegWEn), .clk(clk), .Q(sp));  // open: clr
  Register #(.width(32)) register_3 (.D(D3), .en(RegWEn), .clk(clk), .Q(x3));  // open: clr
  Register #(.width(32)) register_4 (.D(D16), .en(RegWEn), .clk(clk), .Q(x16));  // open: clr
  Register #(.width(32)) register_5 (.D(D17), .en(RegWEn), .clk(clk), .Q(x17));  // open: clr
  Register #(.width(32)) register_6 (.D(D18), .en(RegWEn), .clk(clk), .Q(x18));  // open: clr
  Register #(.width(32)) register_7 (.D(D19), .en(RegWEn), .clk(clk), .Q(x19));  // open: clr
  Register #(.width(32)) register_8 (.D(D4), .en(RegWEn), .clk(clk), .Q(x4));  // open: clr
  Register #(.width(32)) register_9 (.D(D5), .en(RegWEn), .clk(clk), .Q(t0));  // open: clr
  Register #(.width(32)) register_10 (.D(D6), .en(RegWEn), .clk(clk), .Q(t1));  // open: clr
  Register #(.width(32)) register_11 (.D(D7), .en(RegWEn), .clk(clk), .Q(t2));  // open: clr
  Register #(.width(32)) register_12 (.D(D20), .en(RegWEn), .clk(clk), .Q(x20));  // open: clr
  Register #(.width(32)) register_13 (.D(D21), .en(RegWEn), .clk(clk), .Q(x21));  // open: clr
  Register #(.width(32)) register_14 (.D(D22), .en(RegWEn), .clk(clk), .Q(x22));  // open: clr
  Register #(.width(32)) register_15 (.D(D23), .en(RegWEn), .clk(clk), .Q(x23));  // open: clr
  Register #(.width(32)) register_16 (.D(D8), .en(RegWEn), .clk(clk), .Q(s0));  // open: clr
  Register #(.width(32)) register_17 (.D(D9), .en(RegWEn), .clk(clk), .Q(s1));  // open: clr
  Register #(.width(32)) register_18 (.D(D10), .en(RegWEn), .clk(clk), .Q(a0));  // open: clr
  Register #(.width(32)) register_19 (.D(D11), .en(RegWEn), .clk(clk), .Q(x11));  // open: clr
  Register #(.width(32)) register_20 (.D(D24), .en(RegWEn), .clk(clk), .Q(x24));  // open: clr
  Register #(.width(32)) register_21 (.D(D25), .en(RegWEn), .clk(clk), .Q(x25));  // open: clr
  Register #(.width(32)) register_22 (.D(D26), .en(RegWEn), .clk(clk), .Q(x26));  // open: clr
  Register #(.width(32)) register_23 (.D(D27), .en(RegWEn), .clk(clk), .Q(x27));  // open: clr
  Register #(.width(32)) register_24 (.D(D12), .en(RegWEn), .clk(clk), .Q(x12));  // open: clr
  Register #(.width(32)) register_25 (.D(D13), .en(RegWEn), .clk(clk), .Q(x13));  // open: clr
  Register #(.width(32)) register_26 (.D(D14), .en(RegWEn), .clk(clk), .Q(x14));  // open: clr
  Register #(.width(32)) register_27 (.D(D15), .en(RegWEn), .clk(clk), .Q(x15));  // open: clr
  Register #(.width(32)) register_28 (.D(D28), .en(RegWEn), .clk(clk), .Q(x28));  // open: clr
  Register #(.width(32)) register_29 (.D(D29), .en(RegWEn), .clk(clk), .Q(x29));  // open: clr
  Register #(.width(32)) register_30 (.D(D30), .en(RegWEn), .clk(clk), .Q(x30));  // open: clr
  Register #(.width(32)) register_31 (.D(D31), .en(RegWEn), .clk(clk), .Q(x31));  // open: clr
  Demultiplexer #(.select(5), .width(32)) demultiplexer_1 (
    .out0(D0), .out1(D1), .out2(D2), .out3(D3), .out4(D4), .out5(D5), .out6(D6), .out7(D7), .out8(D8),
    .out9(D9), .out10(D10), .out11(D11), .out12(D12), .out13(D13), .out14(D14), .out15(D15), .out16(D16),
    .out17(D17), .out18(D18), .out19(D19), .out20(D20), .out21(D21), .out22(D22), .out23(D23), .out24(D24),
    .out25(D25), .out26(D26), .out27(D27), .out28(D28), .out29(D29), .out30(D30), .out31(D31),
    .in(WriteData), .sel(WriteIndex));
  Multiplexer #(.select(5), .width(32)) multiplexer_1 (
    .in0(x0), .in1(ra), .in2(sp), .in3(x3), .in4(x4), .in5(t0), .in6(t1), .in7(t2), .in8(s0), .in9(s1),
    .in10(a0), .in11(x11), .in12(x12), .in13(x13), .in14(x14), .in15(x15), .in16(x16), .in17(x17),
    .in18(x18), .in19(x19), .in20(x20), .in21(x21), .in22(x22), .in23(x23), .in24(x24), .in25(x25),
    .in26(x26), .in27(x27), .in28(x28), .in29(x29), .in30(x30), .in31(x31), .out(ReadData1), .sel(ReadIndex1));
  Multiplexer #(.select(5), .width(32)) multiplexer_2 (
    .in0(x0), .in1(ra), .in2(sp), .in3(x3), .in4(x4), .in5(t0), .in6(t1), .in7(t2), .in8(s0), .in9(s1),
    .in10(a0), .in11(x11), .in12(x12), .in13(x13), .in14(x14), .in15(x15), .in16(x16), .in17(x17),
    .in18(x18), .in19(x19), .in20(x20), .in21(x21), .in22(x22), .in23(x23), .in24(x24), .in25(x25),
    .in26(x26), .in27(x27), .in28(x28), .in29(x29), .in30(x30), .in31(x31), .out(ReadData2), .sel(ReadIndex2));

  // Notes on the sheet:
  //   INPUTS to your circuit
  //   DON'T CHANGE THE LOCATIONS OF THE INPUTS AND OUTPUTS!
  //   These are DEBUG/TEST outputs from your circuit.
  //   OUTPUTS from your circuit
endmodule
